// Logisim project Contador.circ as structural Verilog: 1 circuit, main circuit Contador
module Contador (
  input  Load,
  input  Enable,
  input  Reloj,
  input  [7:0] Entrada,
  output [7:0] out_5
);

  wire comparator_1_eq, comparator_2_eq, or_1_out;
  wire [7:0] or_2_out;

  or or_1 (or_1_out, Load, comparator_2_eq);
  Counter counter_1 (
    .load(or_1_out), .up(1'b1), .count(Enable), .clk(Reloj), .D(or_2_out), .Q(out_5));  // open: clr, carry
  assign or_2_out = 8'h30 | Entrada;  // OR_Gate or_2, 8 bits wide
  Comparator comparator_1 (.a(8'h34), .b(out_5), .eq(comparator_1_eq));  // open: gt, lt
  Comparator comparator_2 (.a(out_5), .b(8'h37), .eq(comparator_2_eq));  // open: gt, lt

  // Notes on the sheet:
  //   El "Load" setea el 48 o el valor ingresante, el mas grande
  //   Si fuera 55, reseteamos en el proximo tick
  //   if 52 == salida del contador then sumar 52 + 3 (a completar :))
endmodule
