// Logisim project FuncionesF1F2.circ as structural Verilog: 3 circuits, main circuit Funciones
module Funciones (
  input  Z4,
  input  Z3,
  input  Z2,
  input  Z1,
  input  A,
  input  B,
  input  C,
  input  D,
  input  E,
  output F1ANDF2
);

  wire func_f1_1_f1, func_f2_1_f2;

  func_F1 func_f1_1 (.Z4(Z4), .Z3(Z3), .Z2(Z2), .Z1(Z1), .F1(func_f1_1_f1));
  func_F2 func_f2_1 (.A(A), .B(B), .C(C), .D(D), .E(E), .F2(func_f2_1_f2));
  and and_1 (F1ANDF2, func_f1_1_f1, func_f2_1_f2);
endmodule

module func_F1 (
  input  Z4,
  input  Z3,
  input  Z2,
  input  Z1,
  output F1
);

  ROM #(.addrWidth(4), .dataWidth(1)) rom_1 (.addr({Z1, Z2, Z3, Z4}));  // open: data

  // Notes on the sheet:
  //   contents of rom_1 (hex, n*v repeats v):
  //   1 4*0 1 0 0 1 1 0 1 1 0 1 1
endmodule

module func_F2 (
  input  A,
  input  B,
  input  C,
  input  D,
  input  E,
  output F2
);

  wire and_1_out, and_2_out, and_3_out, and_4_out, and_5_out, and_6_out, and_7_out, and_8_out, and_9_out,
       and_10_out, and_11_out, and_12_out, and_13_out, and_14_out, and_15_out, and_16_out, and_17_out,
       and_18_out, and_19_out, and_20_out, and_21_out, and_22_out, and_23_out, and_24_out, and_25_out,
       and_26_out, not_1_out, not_2_out, not_3_out, not_4_out, not_5_out, or_1_out, or_2_out, or_3_out,
       or_4_out, or_5_out, or_6_out, or_8_out;

  not not_1 (not_1_out, A);
  not not_2 (not_2_out, B);
  not not_3 (not_3_out, C);
  not not_4 (not_4_out, D);
  not not_5 (not_5_out, E);
  and and_1 (and_1_out, not_2_out, D);
  and and_2 (and_2_out, not_1_out, B);
  and and_3 (and_3_out, not_3_out, E);
  and and_4 (and_4_out, A, B);
  and and_5 (and_5_out, and_1_out, not_5_out);
  and and_6 (and_6_out, and_2_out, and_3_out);
  and and_7 (and_7_out, B, C);
  and and_8 (and_8_out, not_4_out, not_5_out);
  and and_9 (and_9_out, not_2_out, not_4_out);
  and and_10 (and_10_out, and_4_out, C);
  and and_11 (and_11_out, D, E);
  and and_12 (and_12_out, A, B);
  and and_13 (and_13_out, not_3_out, not_4_out);
  and and_14 (and_14_out, A, B);
  and and_15 (and_15_out, not_3_out, not_5_out);
  and and_16 (and_16_out, not_1_out, not_2_out);
  and and_17 (and_17_out, C, E);
  and and_18 (and_18_out, A, not_2_out);
  and and_19 (and_19_out, not_3_out, E);
  or or_1 (or_1_out, and_5_out, and_6_out);
  and and_20 (and_20_out, and_7_out, and_8_out);
  and and_21 (and_21_out, and_9_out, E);
  and and_22 (and_22_out, and_10_out, and_11_out);
  and and_23 (and_23_out, and_12_out, and_13_out);
  and and_24 (and_24_out, and_14_out, and_15_out);
  and and_25 (and_25_out, and_16_out, and_17_out);
  and and_26 (and_26_out, and_18_out, and_19_out);
  or or_2 (or_2_out, or_1_out, and_20_out);
  or or_3 (or_3_out, and_21_out, and_22_out);
  or or_4 (or_4_out, and_23_out, and_24_out);
  or or_5 (or_5_out, and_25_out, and_26_out);
  or or_6 (or_6_out, or_2_out, or_3_out);
  or or_7 (F2, or_6_out, or_8_out);
  or or_8 (or_8_out, or_4_out, or_5_out);
endmodule
