// Logisim project Proyecto.circ as structural Verilog: 7 circuits, main circuit SUMLAT
module SUMLAT (
  input  Cin,
  input  A7,
  input  A6,
  input  A5,
  input  A4,
  input  A3,
  input  A2,
  input  A1,
  input  A0,
  input  B7,
  input  B6,
  input  B5,
  input  B4,
  input  B3,
  input  B2,
  input  B1,
  input  B0,
  output S7,
  output S6,
  output S5,
  output S4,
  output S3,
  output S2,
  output S1,
  output S0,
  output Cout
);

  wire bloque_b_1_ch, bloque_b_1_cl, bloque_b_1_ghl, bloque_b_1_phl, bloque_b_2_ch, bloque_b_2_cl,
       bloque_b_2_ghl, bloque_b_2_phl, bloque_b_3_ch, bloque_b_3_cl, bloque_b_3_ghl, bloque_b_3_phl,
       bloque_b_4_ch, bloque_b_4_cl, bloque_b_5_ch, bloque_b_5_cl, bloque_b_5_ghl, bloque_b_5_phl,
       bloque_b_6_ch, bloque_b_6_cl, bloque_b_6_ghl, bloque_b_6_phl, bloque_b_7_ch, bloque_b_7_cl,
       bloque_b_7_ghl, bloque_b_7_phl, full_adder_1_g, full_adder_1_p, full_adder_2_g, full_adder_2_p,
       full_adder_3_g, full_adder_3_p, full_adder_4_g, full_adder_4_p, full_adder_5_g, full_adder_5_p,
       full_adder_6_g, full_adder_6_p, full_adder_7_g, full_adder_7_p, full_adder_8_g, full_adder_8_p;

  Full_Adder full_adder_1 (
    .A(A7), .B(B7), .Carry_in(bloque_b_1_ch), .P(full_adder_1_p), .Carry_out(Cout), .S(S7), .G(full_adder_1_g));
  Full_Adder full_adder_2 (
    .A(A6), .B(B6), .Carry_in(bloque_b_1_cl), .P(full_adder_2_p), .S(S6), .G(full_adder_2_g));  // open: Carry_out
  Bloque_B bloque_b_1 (
    .PL(full_adder_2_p), .GL(full_adder_2_g), .Cin(bloque_b_2_ch), .PH(full_adder_1_p), .GH(full_adder_1_g),
    .CH(bloque_b_1_ch), .CL(bloque_b_1_cl), .GHL(bloque_b_1_ghl), .PHL(bloque_b_1_phl));
  Full_Adder full_adder_3 (
    .A(A5), .B(B5), .Carry_in(bloque_b_3_ch), .P(full_adder_3_p), .S(S5), .G(full_adder_3_g));  // open: Carry_out
  Bloque_B bloque_b_2 (
    .PL(bloque_b_3_phl), .GL(bloque_b_3_ghl), .Cin(bloque_b_4_ch), .PH(bloque_b_1_phl), .GH(bloque_b_1_ghl),
    .CH(bloque_b_2_ch), .CL(bloque_b_2_cl), .GHL(bloque_b_2_ghl), .PHL(bloque_b_2_phl));
  Full_Adder full_adder_4 (
    .A(A4), .B(B4), .Carry_in(bloque_b_3_cl), .P(full_adder_4_p), .S(S4), .G(full_adder_4_g));  // open: Carry_out
  Bloque_B bloque_b_3 (
    .PL(full_adder_4_p), .GL(full_adder_4_g), .Cin(bloque_b_2_cl), .PH(full_adder_3_p), .GH(full_adder_3_g),
    .CH(bloque_b_3_ch), .CL(bloque_b_3_cl), .GHL(bloque_b_3_ghl), .PHL(bloque_b_3_phl));
  Full_Adder full_adder_5 (
    .A(A3), .B(B3), .Carry_in(bloque_b_5_ch), .P(full_adder_5_p), .S(S3), .G(full_adder_5_g));  // open: Carry_out
  Bloque_B bloque_b_4 (
    .PL(bloque_b_6_phl), .GL(bloque_b_6_ghl), .Cin(Cin), .PH(bloque_b_2_phl), .GH(bloque_b_2_ghl),
    .CH(bloque_b_4_ch), .CL(bloque_b_4_cl));  // open: GHL, PHL
  Full_Adder full_adder_6 (
    .A(A2), .B(B2), .Carry_in(bloque_b_5_cl), .P(full_adder_6_p), .S(S2), .G(full_adder_6_g));  // open: Carry_out
  Bloque_B bloque_b_5 (
    .PL(full_adder_6_p), .GL(full_adder_6_g), .Cin(bloque_b_6_ch), .PH(full_adder_5_p), .GH(full_adder_5_g),
    .CH(bloque_b_5_ch), .CL(bloque_b_5_cl), .GHL(bloque_b_5_ghl), .PHL(bloque_b_5_phl));
  Full_Adder full_adder_7 (
    .A(A1), .B(B1), .Carry_in(bloque_b_7_ch), .P(full_adder_7_p), .S(S1), .G(full_adder_7_g));  // open: Carry_out
  Bloque_B bloque_b_6 (
    .PL(bloque_b_7_phl), .GL(bloque_b_7_ghl), .Cin(bloque_b_4_cl), .PH(bloque_b_5_phl), .GH(bloque_b_5_ghl),
    .CH(bloque_b_6_ch), .CL(bloque_b_6_cl), .GHL(bloque_b_6_ghl), .PHL(bloque_b_6_phl));
  Full_Adder full_adder_8 (
    .A(A0), .B(B0), .Carry_in(bloque_b_7_cl), .P(full_adder_8_p), .S(S0), .G(full_adder_8_g));  // open: Carry_out
  Bloque_B bloque_b_7 (
    .PL(full_adder_8_p), .GL(full_adder_8_g), .Cin(bloque_b_6_cl), .PH(full_adder_7_p), .GH(full_adder_7_g),
    .CH(bloque_b_7_ch), .CL(bloque_b_7_cl), .GHL(bloque_b_7_ghl), .PHL(bloque_b_7_phl));

  // Other names for the same wires on the sheet: C = Cout

  // Notes on the sheet:
  //   A7B7
  //   A6B6
  //   A5B5
  //   A4B4
  //   A3B3
  //   A2B2
  //   A1B1
  //   A0B0
endmodule

module primer_version (
  input  C0
);

  wire A_p1, A_p2, A_p3, A_p4, A_p5, A_p6, A_p7, A_p8, and_1_out, and_2_out, and_3_out, and_4_out, and_5_out,
       and_6_out, and_7_out, B_p1, B_p2, B_p3, B_p4, B_p5, B_p6, B_p7, B_p8, CH1_out, CH3_2_out, CH3_out,
       CH5_out, CH7_6_out, CH7_out, CH_out, G0_out, G1_0_out, G1_out, G2_out, G3_0_out, G3_2_out, G3_out,
       G4_out, G5_4_out, G5_out, G6_out, G7_4_out, G7_6_out, G7_out, or_1_out, or_2_out, or_3_out, or_4_out,
       or_5_out, or_6_out, or_7_out, P0_out, P1_0_out, P1_out, P2_out, P3_0_out, P3_2_out, P3_out, P4_out,
       P5_4_out, P5_out, P6_out, P7_4_out, P7_6_out, P7_out, xor_1_out, xor_2_out, xor_3_out, xor_4_out,
       xor_5_out, xor_6_out, xor_7_out, xor_8_out;

  // DipSwitch A: pin names not known; wires that end beside it: A_p1, A_p2, A_p3, A_p4, A_p5, A_p6, A_p7, A_p8
  and G7 (G7_out, A_p8, B_p8);
  xor xor_1 (xor_1_out, A_p8, B_p8);
  or P7 (P7_out, A_p8, B_p8);
  // DipSwitch B: pin names not known; wires that end beside it: B_p1, B_p2, B_p3, B_p4, B_p5, B_p6, B_p7, B_p8
  // XOR_Gate S7 has open pins: in0=xor_1_out, in1=CH7_out, out=open
  and P7_6 (P7_6_out, P6_out, P7_out);
  or or_1 (or_1_out, P6_out, G6_out);
  and and_1 (and_1_out, G6_out, P7_out);
  and CH7 (CH7_out, or_1_out, CH7_6_out);
  or G7_6 (G7_6_out, and_1_out, G7_out);
  and G6 (G6_out, A_p7, B_p7);
  xor xor_2 (xor_2_out, A_p7, B_p7);
  or P6 (P6_out, A_p7, B_p7);
  // XOR_Gate S6 has open pins: in0=xor_2_out, in1=CH7_6_out, out=open
  and P7_4 (P7_4_out, P5_4_out, P7_6_out);
  and and_2 (and_2_out, G5_4_out, P7_6_out);
  or or_2 (or_2_out, P4_out, G4_out);
  or G7_4 (G7_4_out, and_2_out, G7_6_out);
  xor xor_3 (xor_3_out, A_p6, B_p6);
  and CH5 (CH5_out, or_2_out, CH_out);
  or or_3 (or_3_out, P5_4_out, G5_4_out);
  // XOR_Gate S5 has open pins: in0=xor_3_out, in1=CH5_out, out=open
  or P5 (P5_out, A_p6, B_p6);
  and G5 (G5_out, A_p6, B_p6);
  and CH7_6 (CH7_6_out, or_3_out, CH_out);
  and P5_4 (P5_4_out, P4_out, P5_out);
  and and_3 (and_3_out, G4_out, P5_out);
  xor xor_4 (xor_4_out, A_p5, B_p5);
  or G5_4 (G5_4_out, and_3_out, G5_out);
  // XOR_Gate S4 has open pins: in0=xor_4_out, in1=CH_out, out=open
  or P4 (P4_out, A_p5, B_p5);
  and G4 (G4_out, A_p5, B_p5);
  xor xor_5 (xor_5_out, A_p4, B_p4);
  // XOR_Gate S3 has open pins: in0=xor_5_out, in1=CH3_out, out=open
  or P3 (P3_out, A_p4, B_p4);
  and G3 (G3_out, A_p4, B_p4);
  or or_4 (or_4_out, P2_out, G2_out);
  // AND_Gate P7_0 has open pins: in0=P3_0_out, in1=P7_4_out, out=open
  and and_4 (and_4_out, G3_0_out, P7_4_out);
  and CH3 (CH3_out, or_4_out, CH3_2_out);
  // OR_Gate G7_0 has open pins: in0=and_4_out, in1=G7_4_out, out=open
  or or_5 (or_5_out, P3_0_out, G3_0_out);
  and P3_2 (P3_2_out, P2_out, P3_out);
  and and_5 (and_5_out, G2_out, P3_out);
  and CH (CH_out, or_5_out, C0);
  or G3_2 (G3_2_out, and_5_out, G3_out);
  xor xor_6 (xor_6_out, A_p3, B_p3);
  // XOR_Gate S2 has open pins: in0=xor_6_out, in1=CH3_2_out, out=open
  or or_6 (or_6_out, P1_0_out, G1_0_out);
  or P2 (P2_out, A_p3, B_p3);
  and G2 (G2_out, A_p3, B_p3);
  and CH3_2 (CH3_2_out, or_6_out, C0);
  and P3_0 (P3_0_out, P1_0_out, P3_2_out);
  and and_6 (and_6_out, G1_0_out, P3_2_out);
  or or_7 (or_7_out, P0_out, G0_out);
  xor xor_7 (xor_7_out, A_p2, B_p2);
  and CH1 (CH1_out, or_7_out, C0);
  or G3_0 (G3_0_out, and_6_out, G3_2_out);
  // XOR_Gate S1 has open pins: in0=xor_7_out, in1=CH1_out, out=open
  or P1 (P1_out, A_p2, B_p2);
  and G1 (G1_out, A_p2, B_p2);
  and P1_0 (P1_0_out, P0_out, P1_out);
  and and_7 (and_7_out, G0_out, P1_out);
  xor xor_8 (xor_8_out, A_p1, B_p1);
  or G1_0 (G1_0_out, and_7_out, G1_out);
  // XOR_Gate S0 has open pins: in0=xor_8_out, in1=C0, out=open
  or P0 (P0_out, A_p1, B_p1);
  and G0 (G0_out, A_p1, B_p1);

  // Notes on the sheet:
  //   Cin
  //   FA7
  //   PL
  //   PH
  //   GL
  //   GH
  //   Cin
  //   CL
  //   Cin
  //   FA6
  //   PH
  //   Cin
  //   GL
  //   GH
  //   FA5
  //   PL
  //   Cin
  //   CL
  //   Cin
  //   Cin
  //   PL
  //   PH
  //   GH
  //   GL
  //   FA4
  //   Los C de cada FA son los Cin que están diagramados en el PDF del proyecto, es decir, dependen de los niveles más altos, hay que unirlos cuando estén hechos
  //   Cin
  //   CL
  //   FA3
  //   PH
  //   GH
  //   PL
  //   GL
  //   Cin
  //   PL
  //   PH
  //   CL
  //   GL
  //   GH
  //   FA2
  //   CL
  //   Cin
  //   Cin
  //   PH
  //   PL
  //   GL
  //   GH
  //   Cin
  //   CL
  //   FA1
  //   Cin
  //   Cin
  //   PL
  //   PH
  //   GL
  //   GH
  //   CL
  //   FA0
endmodule

module Full_Adder (
  input  A,
  input  B,
  input  Carry_in,
  output P,
  output Carry_out,
  output S,
  output G
);

  wire and_2_out, xor_1_out;

  or or_1 (P, A, B);
  xor xor_1 (xor_1_out, A, B);
  and and_1 (G, B, A);
  and and_2 (and_2_out, P, Carry_in);
  or or_2 (Carry_out, and_2_out, G);
  xor xor_2 (S, xor_1_out, Carry_in);

  // Other names for the same wires on the sheet: O = G; X = Carry_in

  // Notes on the sheet:
  //   P0
endmodule

module Bloque_B (
  input  PH,
  input  GH,
  input  PL,
  input  GL,
  input  Cin,
  output GHL,
  output PHL,
  output CH,
  output CL
);

  wire and_1_out, and_3_out;

  and and_1 (and_1_out, PH, GL);
  and and_2 (PHL, PH, PL);
  and and_3 (and_3_out, PL, Cin);
  or or_1 (GHL, GH, and_1_out);
  or or_2 (CH, GL, and_3_out);

  assign CL = Cin;
endmodule

module prueba_SUMLAT (
  input  Cin,
  input  [7:0] A,
  input  [7:0] B,
  output [7:0] S_decimal,
  output Cout
);

  SUMLAT sumlat_1 (
    .Cin(Cin), .A7(A[7]), .A6(A[6]), .A5(A[5]), .A4(A[4]), .A3(A[3]), .A2(A[2]), .A1(A[1]), .A0(A[0]),
    .B7(B[7]), .B6(B[6]), .B5(B[5]), .B4(B[4]), .B3(B[3]), .B2(B[2]), .B1(B[1]), .B0(B[0]),
    .S7(S_decimal[7]), .S6(S_decimal[6]), .S5(S_decimal[5]), .S4(S_decimal[4]), .S3(S_decimal[3]),
    .S2(S_decimal[2]), .S1(S_decimal[1]), .S0(S_decimal[0]), .Cout(Cout));

  // Notes on the sheet:
  //   Como entrada pasamos el valor en decimal y automaticamente se pasa a binario
  //   Para ingresarlo hay que ir a las propiedades y en la parte de "Valor" lo ingresamos, lo van a ver en Hexa pero lo ingresan en decimal
endmodule

module Sumador_y_contador (
  input  [7:0] in_1,
  input  [7:0] in_2,
  input  [7:0] in_3,
  output out_4,
  output out_5,
  output out_6,
  output out_7,
  output out_8,
  output out_9,
  output out_10,
  output out_11
);

  wire clock_1_out, comparator_1_eq, comparator_1_gt;
  wire [7:0] multiplexer_1_out, undriven;

  Clock clock_1 (.out(clock_1_out));
  Comparator comparator_1 (
    .a({undriven[7:2], undriven[2], undriven[0]}), .b(in_3), .gt(comparator_1_gt), .eq(comparator_1_eq));  // open: lt
  Multiplexer #(.width(8)) multiplexer_1 (.in0(in_1), .in1(in_2), .out(multiplexer_1_out), .sel(comparator_1_eq));
  SUMLAT sumlat_1 (
    .Cin(undriven[7]), .A7(undriven[6]), .A6(undriven[5]), .A5(undriven[4]), .A4(undriven[3]),
    .A3(undriven[2]), .A2(undriven[2]), .A1(undriven[0]), .A0(multiplexer_1_out[7]),
    .B7(multiplexer_1_out[6]), .B6(multiplexer_1_out[5]), .B5(multiplexer_1_out[4]),
    .B4(multiplexer_1_out[3]), .B3(multiplexer_1_out[2]), .B2(multiplexer_1_out[1]),
    .B1(multiplexer_1_out[0]), .S7(out_4), .S6(out_5), .S5(out_6), .S4(out_7), .S3(out_8), .S2(out_9),
    .S1(out_10), .S0(out_11));  // open: B0, Cout
endmodule

module Contador_1 (
  input  Z4,
  input  Z3,
  input  Z2,
  input  Z1,
  input  A,
  input  B,
  input  C,
  input  D,
  input  E,
  output [7:0] ESTADO
);

  wire and_1_out, and_2_out, bcd_to_7_segment_decoder_2_p1, binary_to_bcd_converter_1_p2, clock_1_out,
       Comparador_0_out, Comparador_48_out, Comparador_49_out, Comparador_52_out, Comparador_55_out,
       funciones_1_f1andf2, not_1_out, not_2_out, not_3_out, not_4_out, not_5_out, not_6_out, not_7_out,
       not_8_out, not_9_out, not_10_out, not_11_out, not_12_out, not_13_out, not_14_out, not_15_out,
       not_16_out, not_17_out, not_18_out, not_19_out, not_20_out, not_21_out, not_22_out, not_23_out,
       not_24_out, not_25_out, not_26_out, not_27_out, or_1_out, Saltos_out;
  wire [7:0] multiplexer_1_out, sumlat_1_s0;

  Multiplexer #(.width(8)) multiplexer_1 (.in0(sumlat_1_s0), .in1(8'h30), .out(multiplexer_1_out), .sel(or_1_out));
  Clock clock_1 (.out(clock_1_out));
  Counter Contador (
    .load(Saltos_out), .up(1'b1), .count(1'b1), .clk(clock_1_out), .D(multiplexer_1_out), .Q(ESTADO));  // open: clr, carry
  // Binary_to_BCD_converter #(.binvalue(8)) binary_to_bcd_converter_1: pin names not known; wires that end beside it: ESTADO, binary_to_bcd_converter_1_p2
  _7_Segment_Display u_7_segment_display_1 ();  // open: g, f, a, b, e, d, c, dp
  // BCD_to_7_Segment_decoder bcd_to_7_segment_decoder_1: pin names not known; wires that end beside it: binary_to_bcd_converter_1_p2
  _7_Segment_Display u_7_segment_display_2 ();  // open: g, f, a, b, e, d, c, dp
  // BCD_to_7_Segment_decoder bcd_to_7_segment_decoder_2: pin names not known; wires that end beside it: bcd_to_7_segment_decoder_2_p1, bcd_to_7_segment_decoder_2_p1
  SUMLAT sumlat_1 (
    .A7(ESTADO[7]), .A6(ESTADO[6]), .A5(ESTADO[5]), .A4(ESTADO[4]), .A3(ESTADO[3]), .A2(ESTADO[2]),
    .A1(ESTADO[1]), .A0(ESTADO[0]), .B7(1'b0), .B6(1'b0), .B5(1'b0), .B4(1'b0), .B3(1'b0), .B2(1'b0),
    .B1(1'b1), .B0(1'b1), .S7(sumlat_1_s0[7]), .S6(sumlat_1_s0[6]), .S5(sumlat_1_s0[5]), .S4(sumlat_1_s0[4]),
    .S3(sumlat_1_s0[3]), .S2(sumlat_1_s0[2]), .S1(sumlat_1_s0[1]), .S0(sumlat_1_s0[0]));  // open: Cin, Cout
  not not_1 (not_1_out, ESTADO[0]);
  not not_2 (not_2_out, ESTADO[7]);
  not not_3 (not_3_out, ESTADO[6]);
  not not_4 (not_4_out, ESTADO[5]);
  not not_5 (not_5_out, ESTADO[4]);
  not not_6 (not_6_out, ESTADO[3]);
  not not_7 (not_7_out, ESTADO[2]);
  not not_8 (not_8_out, ESTADO[1]);
  not not_9 (not_9_out, ESTADO[0]);
  not not_10 (not_10_out, ESTADO[1]);
  not not_11 (not_11_out, ESTADO[2]);
  not not_12 (not_12_out, ESTADO[3]);
  not not_13 (not_13_out, ESTADO[6]);
  not not_14 (not_14_out, ESTADO[7]);
  not not_15 (not_15_out, ESTADO[1]);
  not not_16 (not_16_out, ESTADO[2]);
  not not_17 (not_17_out, ESTADO[3]);
  not not_18 (not_18_out, ESTADO[6]);
  not not_19 (not_19_out, ESTADO[7]);
  not not_20 (not_20_out, ESTADO[0]);
  not not_21 (not_21_out, ESTADO[1]);
  not not_22 (not_22_out, ESTADO[3]);
  not not_23 (not_23_out, ESTADO[6]);
  not not_24 (not_24_out, ESTADO[7]);
  not not_25 (not_25_out, ESTADO[3]);
  not not_26 (not_26_out, ESTADO[6]);
  not not_27 (not_27_out, ESTADO[7]);
  and Comparador_49 (Comparador_49_out, ESTADO[0], not_15_out, not_16_out, not_17_out, ESTADO[4], ESTADO[5], not_18_out, not_19_out);
  and Comparador_52 (Comparador_52_out, not_20_out, not_21_out, ESTADO[2], not_22_out, ESTADO[4], ESTADO[5], not_23_out, not_24_out);
  and Comparador_55 (Comparador_55_out, ESTADO[0], ESTADO[1], ESTADO[2], not_25_out, ESTADO[4], ESTADO[5], not_26_out, not_27_out);
  and Comparador_0 (Comparador_0_out, not_2_out, not_3_out, not_4_out, not_5_out, not_6_out, not_7_out, not_8_out, not_9_out);
  and Comparador_48 (Comparador_48_out, not_1_out, not_10_out, not_11_out, not_12_out, ESTADO[4], ESTADO[5], not_13_out, not_14_out);
  or or_1 (or_1_out, Comparador_55_out, Comparador_0_out);
  or Saltos (Saltos_out, Comparador_0_out, Comparador_52_out, Comparador_55_out, and_1_out, and_2_out);
  and and_1 (and_1_out, Comparador_48_out, funciones_1_f1andf2);
  and and_2 (and_2_out, Comparador_49_out, funciones_1_f1andf2);
  Funciones funciones_1 (
    .Z4(Z4), .Z3(Z3), .Z2(Z2), .Z1(Z1), .A(A), .B(B), .C(C), .D(D), .E(E), .F1ANDF2(funciones_1_f1andf2));

  // Notes on the sheet:
  //   Enable
  //   Clock
  //   Si debo saltar, verifico
  //   o si es para reiniciar el circuito
  //   Siempre le sumo 3 al estado actual por si debo saltar
  //   Aca compruebo si debo aplicar salto (activar load)
endmodule
